# Fritzing sketch fritzing_gps (saved by Fritzing 0.9.3b)

parts:
  Composant1 = Generic GPS
  Composant2 = Arduino Uno (Rev3)  # not connected
  Composant3 = Base Shield V2

nets:
  N1: Composant1.RX, Composant3.pin_98
  N2: Composant1.TX, Composant3.pin_99
  N3: Composant1.GND, Composant3.pin_96
  N4: Composant1.VCC, Composant3.pin_97
